# Fritzing sketch soil moisture sensor (saved by Fritzing 0.9.3b)
breadboards: 1

parts:
  Part2 = Arduino Uno (Rev3) - ICSP
  Part3 = LCD1602-I2C
  Part4 = Soil Moisture Sensor
  WATER_PUMP1 = water pump/motor  # not connected
  BAT1 = BC9VPC [package=bc9vpc]
  KY-1 = Keyes Relay [package=THT]

nets:
  N1: Part2.A0, Part4.SIG
  N2: Part2.A4/SDA, Part3.SDA
  N3: Part2.A5/SCL, Part3.SCL
  VCC: Part2.5V, Part3.VCC, Part4.VCC, KY-1.power
  GND: Part2.GND, Part3.GND, Part4.GND, BAT1.V-, KY-1.ground, KY-1.NC
  N4: Part2.D2, KY-1.signal
  N5: Part2.VIN, BAT1.V+

custom parts:
  LCD1602-I2C: A standard character display, usually with 2x16 characters. Comes in many colors with LCM1602 IIC attached.
  water pump/motor: WATER PUMP BY ARDUBLOCKTR
  Keyes Relay: The Keyes 5V relay module is suitable for SCM development, home appliance control. It uses a 5V~12V TIL control signal which can control DC / AC signal.
